// Digital circuit Instruction Decoder.dig as structural Verilog
module Instruction_Decoder (
  input  CLK,
  input  I0,
  input  I1,
  input  I2,
  input  I3,
  input  I4,
  input  I5,
  input  I6,
  input  I7,
  input  F0,
  input  FN,
  input  FC,
  output HLT,
  output M_R,
  output M_W,
  output M_PL,
  output M_PH,
  output M_PI,
  output O_W,
  output ALU_E,
  output ALU_NB,
  output ALU_C,
  output ALU_AND,
  output ALU_OR,
  output ALU_NOT,
  output ALU_LS,
  output ALU_SUM,
  output W_R,
  output W_W,
  output X_R,
  output X_W,
  output Y_R,
  output Y_W,
  output Z_R,
  output Z_W,
  output I_W,
  output PC_E,
  output PC_R,
  output PC_W,
  output FL_W
);

  wire and_1_out, counter_1_ovf, not_1_out, not_2_out;
  wire [2:0] counter_1_out;
  wire [31:28] rom_1_d;

  not not_1 (not_1_out, CLK);
  Counter #(.Bits(3)) counter_1 (
    .en(not_1_out), .C(not_1_out), .clr(and_1_out), .out(counter_1_out), .ovf(counter_1_ovf));
  LED led_1 (.in(counter_1_ovf));
  not not_2 (not_2_out, counter_1_out[1]);
  and and_1 (and_1_out, counter_1_out[0], not_2_out, counter_1_out[2]);
  ROM #(.AddrBits(14), .Bits(32)) rom_1 (
    .A({FC, FN, F0, I7, I6, I5, I4, I3, I2, I1, I0, counter_1_out}), .sel(1'b1),
    .D({rom_1_d, FL_W, PC_W, PC_R, PC_E, I_W, Z_W, Z_R, Y_W, Y_R, X_W, X_R, W_W, W_R, ALU_SUM, ALU_LS, ALU_NOT, ALU_OR, ALU_AND, ALU_NB, ALU_C, ALU_E, O_W, M_PI, M_PH, M_PL, M_W, M_R, HLT}));
endmodule
